// Logisim project cpu_benchmark.circ as structural Verilog: 8 circuits, main circuit cpu
module cpu (
);

  wire and_1_out, clock_1_out, control_1_output__alu_y, control_1_output__extend_i_iu,
       control_1_output__ifjump, control_1_output__npc_chose_off_new, control_1_output__npc_newpc_r1_lable,
       control_1_output__npc_offset_0_extend, control_1_output__readmemory,
       control_1_output__rf_r1_rs_0_rt_1, control_1_output__rf_w_1_able, control_1_output__rf_wf_rd_rt,
       control_1_output__writememory, nand_1_out, RST;
  wire [1:0] control_1_output__decoder_signal, control_1_output__extend_chose,
       control_1_output__extend_offset, control_1_output__rf_din_alu_dm_npc;
  wire [3:0] control_1_output__alu_op, control_1_output__rf_din_alu_dm_npc_2;
  wire [4:0] decode_1_output__rd, decode_1_output__rs, decode_1_output__rt, multiplexer_2_out,
       multiplexer_3_out;
  wire [15:0] adder_1_out, counter_3_out, \总周期数 , \无条件分支指令数 , \有条件分支成功跳转 , \有条件分支指令数 ;
  wire [25:0] decode_1_output__im26;
  wire [31:0] alu_1_out_4, bit_extender_1_out, extend_1_output, mips_ram_1_p8, multiplexer_4_out,
       multiplexer_5_out, multiplexer_6_out, npc_1_output__new_pc, npc_1_output__pc___4, register_1_q,
       register_3_output__r1, register_3_output__r2, rom_1_data, SyscallOut;

  Button \u_总复位  (.out(RST));
  Clock clock_1 (.out(clock_1_out));
  Multiplexer #(.width(16)) multiplexer_1 (
    .in0(adder_1_out), .in1(counter_3_out), .out(\总周期数 ), .sel(nand_1_out));  // open: en
  Counter counter_1 (.in(control_1_output__npc_chose_off_new), .out(\无条件分支指令数 ), .clk(clock_1_out));
  Hex_Digit_Display hex_digit_display_1 (.value(SyscallOut[27:24]));  // open: dp
  Hex_Digit_Display hex_digit_display_2 (.value(SyscallOut[31:28]));  // open: dp
  Register #(.width(32)) register_1 (
    .D(npc_1_output__new_pc), .en(nand_1_out), .Q(register_1_q), .clk(clock_1_out));  // open: clr
  Counter counter_2 (.in(control_1_output__npc_offset_0_extend), .out(\有条件分支成功跳转 ), .clk(clock_1_out));
  Adder #(.width(16)) adder_1 (.a(16'h1), .b(counter_3_out), .out(adder_1_out));  // open: cin, cout
  Hex_Digit_Display hex_digit_display_3 (.value(SyscallOut[19:16]));  // open: dp
  Hex_Digit_Display hex_digit_display_4 (.value(SyscallOut[23:20]));  // open: dp
  Register #(.width(32)) register_2 (
    .D(register_3_output__r2), .en(control_1_output__decoder_signal[0]), .Q(SyscallOut), .clk(clock_1_out));  // open: clr
  Counter counter_3 (.in(nand_1_out), .out(counter_3_out), .clk(clock_1_out));
  Hex_Digit_Display hex_digit_display_5 (.value(SyscallOut[15:12]));  // open: dp
  Hex_Digit_Display hex_digit_display_6 (.value(SyscallOut[11:8]));  // open: dp
  nand nand_1 (nand_1_out, control_1_output__decoder_signal[0], alu_1_out_4[0]);
  Counter counter_4 (.in(control_1_output__ifjump), .out(\有条件分支指令数 ), .clk(clock_1_out));
  Hex_Digit_Display hex_digit_display_7 (.value(SyscallOut[7:4]));  // open: dp
  Hex_Digit_Display hex_digit_display_8 (.value(SyscallOut[3:0]));  // open: dp
  ROM #(.addrWidth(24), .dataWidth(32)) rom_1 (.addr(register_1_q[25:2]), .data(rom_1_data));  // open: sel
  // Probe on \总周期数 
  // Probe on \无条件分支指令数 
  // Probe on \有条件分支指令数 
  // Probe on \有条件分支成功跳转 
  control control_1 (
    .Input__im(rom_1_data), .input__alu_equal(alu_1_out_4[0]), .output__Alu_y(control_1_output__alu_y),
    .output__RF_W_1_able(control_1_output__rf_w_1_able),
    .output__npc_offset_0_Extend(control_1_output__npc_offset_0_extend),
    .output__extend_i_iu(control_1_output__extend_i_iu), .output__Alu_op(control_1_output__alu_op),
    .output__RF_R1_RS_0_RT_1(control_1_output__rf_r1_rs_0_rt_1),
    .output__npc_newpc_R1_lable(control_1_output__npc_newpc_r1_lable),
    .output__extend_chose(control_1_output__extend_chose),
    .output__RF_WF_RD_RT(control_1_output__rf_wf_rd_rt),
    .output__npc_chose_Off_new(control_1_output__npc_chose_off_new),
    .output__extend_offset(control_1_output__extend_offset),
    .output__RF_Din_alu_dm_NPC(control_1_output__rf_din_alu_dm_npc),
    .output__decoder_signal(control_1_output__decoder_signal), .output__IfJump(control_1_output__ifjump),
    .output__WriteMemory(control_1_output__writememory), .output__ReadMemory(control_1_output__readmemory),
    .output__RF_Din_alu_dm_NPC_2(control_1_output__rf_din_alu_dm_npc_2));
  Decode decode_1 (
    .input__IF(rom_1_data), .output__RS(decode_1_output__rs), .output__RT(decode_1_output__rt),
    .output__RD(decode_1_output__rd), .output__im26(decode_1_output__im26),
    .input__Signal_ord_syscall_jal(control_1_output__decoder_signal));
  extend extend_1 (
    .input__26bit(decode_1_output__im26), .input__offset(control_1_output__extend_offset),
    .input__i_iu(control_1_output__extend_i_iu), .input__chose(control_1_output__extend_chose),
    .\output (extend_1_output));
  // Probe on multiplexer_3_out
  // Probe on multiplexer_4_out
  npc npc_1 (
    .input__npc_extend(extend_1_output), .input__npc_r1(register_3_output__r1),
    .input__npc_old_pc(register_1_q), .input__signal_chose(control_1_output__npc_chose_off_new),
    .input__signal_npc_offset(control_1_output__npc_offset_0_extend),
    .input__signal_npc_new_pc(control_1_output__npc_newpc_r1_lable), .output__pc___4(npc_1_output__pc___4),
    .output__new_pc(npc_1_output__new_pc));
  // Probe on decode_1_output__rt
  Multiplexer #(.width(5)) multiplexer_2 (
    .in0(decode_1_output__rs), .in1(decode_1_output__rt), .out(multiplexer_2_out),
    .sel(control_1_output__rf_r1_rs_0_rt_1));  // open: en
  Multiplexer #(.width(5)) multiplexer_3 (
    .in0(decode_1_output__rt), .in1(decode_1_output__rd), .out(multiplexer_3_out),
    .sel(control_1_output__rf_wf_rd_rt));  // open: en
  register register_3 (
    .Input__R1(multiplexer_2_out), .Input__Din(multiplexer_4_out), .Input__R2(decode_1_output__rt),
    .Input__W(control_1_output__rf_w_1_able), .Input__Rw(multiplexer_3_out),
    .output__R1(register_3_output__r1), .output__R2(register_3_output__r2), .clk(clock_1_out));
  // Probe on register_3_output__r1
  Multiplexer #(.select(2), .width(32)) multiplexer_4 (
    .in0(alu_1_out_4), .in1(multiplexer_6_out), .in2(npc_1_output__pc___4), .out(multiplexer_4_out),
    .sel(control_1_output__rf_din_alu_dm_npc));  // open: in3, en
  // Probe on register_3_output__r2
  // Probe on multiplexer_4_out
  Multiplexer #(.width(32)) multiplexer_5 (
    .in0(register_3_output__r2), .in1(extend_1_output), .out(multiplexer_5_out), .sel(control_1_output__alu_y));  // open: en
  // Probe on alu_1_out_4
  Alu alu_1 (
    .in_1(register_3_output__r1), .in_2(multiplexer_5_out), .out_4(alu_1_out_4),
    .in_3(control_1_output__alu_op));
  // Probe on control_1_output__alu_op
  // MIPS_RAM mips_ram_1: pin names not known; wires that end beside it: alu_1_out_4, alu_1_out_4[25:2], register_3_output__r2, control_1_output__writememory, control_1_output__rf_din_alu_dm_npc_2, clock_1_out, control_1_output__readmemory, mips_ram_1_p8
  assign bit_extender_1_out = {{24{1'b0}}, mips_ram_1_p8[7:0]};  // Bit_Extender bit_extender_1
  and and_1 (and_1_out, control_1_output__rf_din_alu_dm_npc_2[0], ~control_1_output__rf_din_alu_dm_npc_2[1], ~control_1_output__rf_din_alu_dm_npc_2[2], ~control_1_output__rf_din_alu_dm_npc_2[3]);  // AND_Gate
  Multiplexer #(.width(32)) multiplexer_6 (
    .in0(mips_ram_1_p8), .in1(bit_extender_1_out), .out(multiplexer_6_out), .sel(and_1_out));  // open: en

  // Notes on the sheet:
  //   数码管输出应该用寄存器锁存，否则显示数据只能一闪而过
  //   可以通过项目增加Logisim库的方式将前几次实验完成的电路作为子电路引入到本电路中使用
  //   数码管输出
  //   contents of rom_1 (hex, n*v repeats v):
  //   20110001 8000005 20110001 20120002 20130003 8000009 20110001 20120002 20130003 800000d 20110001
  //   20120002 20130003 8000011 20110001 20120002 20130003 c0000b8 20100001 20110001 118fc0 112020
  //   20020022 c 118882 12200001 8000015 112020 20020022 c 20110001 118880 112020 20020022 c 12200001
  //   800001f 20110001 118fc0 112020 20020022 c 1188c3 112020 20020022 c 118903 112020 20020022 c 118903
  //   112020 20020022 c 118903 112020 20020022 c 118903 112020 20020022 c 118903 112020 20020022 c 118903
  //   112020 20020022 c 118903 112020 20020022 c 20100001 109fc0 139fc3 8021 2012000c 24160003 26100001
  //   3210000f 20080008 20090001 139900 2709825 132020 20020022 c 1094022 1500fff9 22100001 2018000f
  //   2188024 108700 20080008 20090001 139902 2709825 132021 20020022 c 1094022 1500fff9 108702 2c9b022
  //   12c00001 8000050 4020 1084027 84400 3508ffff 82021 20020022 c 2010ffff 20110000 ae300000 22100001
  //   22310004 ae300000 22100001 22310004 ae300000 22100001 22310004 ae300000 22100001 22310004 ae300000
  //   22100001 22310004 ae300000 22100001 22310004 ae300000 22100001 22310004 ae300000 22100001 22310004
  //   ae300000 22100001 22310004 ae300000 22100001 22310004 ae300000 22100001 22310004 ae300000 22100001
  //   22310004 ae300000 22100001 22310004 ae300000 22100001 22310004 ae300000 22100001 22310004 ae300000
  //   22100001 22310004 22100001 8020 2011003c 8e130000 8e340000 274402a 11000002 ae330000 ae140000
  //   2231fffc 1611fff8 102020 20020022 c 22100004 2011003c 1611fff2 2002000a c 20100000 22100001 102020
  //   20020022 c 22100002 102020 20020022 c 22100003 102020 20020022 c 22100004 102020 20020022 c 22100005
  //   102020 20020022 c 22100006 102020 20020022 c 22100007 102020 20020022 c 22100008 102020 20020022
  //   20020022 c 3e00008
  //   总复位信号应将除ROM以外所有存储组件全部清零
endmodule

// NPCOffset
module npc (
  input  [31:0] input__npc_extend,
  input  [31:0] input__npc_r1,
  input  [31:0] input__npc_old_pc,
  input  input__signal_chose,
  input  input__signal_npc_offset,
  input  input__signal_npc_new_pc,
  output [31:0] output__pc___4,
  output [31:0] output__new_pc
);

  wire [31:0] adder_1_out, multiplexer_1_out, multiplexer_2_out;

  Multiplexer #(.width(32)) multiplexer_1 (
    .in0({32{1'b0}}), .in1(input__npc_extend), .out(multiplexer_1_out), .sel(input__signal_npc_offset));  // open: en
  Multiplexer #(.width(32)) multiplexer_2 (
    .in0(input__npc_r1), .in1({input__npc_old_pc[31:28], input__npc_extend[27:0]}), .out(multiplexer_2_out),
    .sel(input__signal_npc_new_pc));  // open: en
  Adder #(.width(32)) adder_1 (.a(multiplexer_1_out), .b(32'h4), .out(adder_1_out));  // open: cin, cout
  Adder #(.width(32)) adder_2 (.a(adder_1_out), .b(input__npc_old_pc), .out(output__pc___4));  // open: cin, cout
  Multiplexer #(.width(32)) multiplexer_3 (
    .in0(output__pc___4), .in1(multiplexer_2_out), .out(output__new_pc), .sel(input__signal_chose));  // open: en

  // Other names for the same wires on the sheet: NPCExtend[31:0] = input__npc_extend; OldPC[31:0] = input__npc_old_pc;
  //   NewPC[31:0] = output__new_pc; NPCChose = input__signal_chose; NPCNewPC = input__signal_npc_new_pc;
  //   NPCOff[31:0] = output__pc___4; NPCOffset = input__signal_npc_offset; NPCR1[31:0] = input__npc_r1
endmodule

// Control
module control (
  input  [31:0] Input__im,
  input  input__alu_equal,
  output output__Alu_y,
  output [3:0] output__Alu_op,
  output output__RF_W_1_able,
  output output__RF_R1_RS_0_RT_1,
  output output__RF_WF_RD_RT,
  output [1:0] output__RF_Din_alu_dm_NPC,
  output output__npc_offset_0_Extend,
  output output__npc_newpc_R1_lable,
  output output__npc_chose_Off_new,
  output [3:0] output__RF_Din_alu_dm_NPC_2,
  output output__extend_i_iu,
  output [1:0] output__extend_chose,
  output [1:0] output__extend_offset,
  output [1:0] output__decoder_signal,
  output output__IfJump,
  output output__WriteMemory,
  output output__ReadMemory
);

  wire Add, add_out, Addi, AddiU, AddU, And, And_4_out, and_25_out, and_26_out, Andi, Beq, Bne, Bqtz,
       Class_R, Cmp_out, Equ_out, J, Jr, Lb, Lw, Nor, Or, or_1_out, OR_3_out, or_4_out, or_5_out, or_7_out,
       or_10_out, or_12_out, Ori, Sll, Slt, Slti, SltU, Sra, Srl, Sub, Sub_out, SubU;
  wire [3:0] OP0_out;

  and and_1 (Class_R, ~Input__im[26], ~Input__im[27], ~Input__im[28], ~Input__im[29], ~Input__im[30], ~Input__im[31]);  // AND_Gate
  Multiplexer #(.width(4)) multiplexer_1 (.in0(OP0_out), .in1(4'b1111), .out(output__Alu_op), .sel(Bqtz));  // open: en
  and and_2 (J, ~Input__im[26], Input__im[27], ~Input__im[28], ~Input__im[29], ~Input__im[30], ~Input__im[31]);  // AND_Gate
  and and_3 (Sll, Class_R, ~Input__im[0], ~Input__im[1], ~Input__im[2], ~Input__im[3], ~Input__im[4], ~Input__im[5]);  // AND_Gate
  or or_1 (or_1_out, Slti, Andi, Ori, output__extend_offset[1], Lb, Lw);
  or or_2 (output__RF_Din_alu_dm_NPC[0], Lb, Lw);
  or u_add (add_out, Addi, AddiU, Add, AddU, Lb, Lw, output__WriteMemory);
  or u_Sub (Sub_out, Sub, SubU);
  or And_4 (And_4_out, And, Andi);
  or OR_3 (OR_3_out, Or, output__extend_offset[1], Ori);
  or Cmp (Cmp_out, Slt, Slti);
  or Equ (Equ_out, output__decoder_signal[0], Beq, Bne);
  and and_5 (output__decoder_signal[1], Input__im[26], Input__im[27], ~Input__im[28], ~Input__im[29], ~Input__im[30], ~Input__im[31]);  // AND_Gate
  and and_6 (Srl, Class_R, ~Input__im[0], Input__im[1], ~Input__im[2], ~Input__im[3], ~Input__im[4], ~Input__im[5]);  // AND_Gate
  or OP0 (OP0_out[0], Sra, add_out, And_4_out, Cmp_out, Equ_out);
  and and_7 (Beq, ~Input__im[26], ~Input__im[27], Input__im[28], ~Input__im[29], ~Input__im[30], ~Input__im[31]);  // AND_Gate
  and and_8 (Sra, Class_R, Input__im[0], Input__im[1], ~Input__im[2], ~Input__im[3], ~Input__im[4], ~Input__im[5]);  // AND_Gate
  or OP2 (OP0_out[2], add_out, Sub_out, And_4_out, SltU, Equ_out);
  or OP1 (OP0_out[1], Srl, Sub_out, And_4_out, Nor, Cmp_out);
  and and_9 (Bne, Input__im[26], ~Input__im[27], Input__im[28], ~Input__im[29], ~Input__im[30], ~Input__im[31]);  // AND_Gate
  and and_10 (Jr, Class_R, ~Input__im[0], ~Input__im[1], ~Input__im[2], Input__im[3], ~Input__im[4], ~Input__im[5]);  // AND_Gate
  or or_4 (or_4_out, Sll, Srl, Sra, output__decoder_signal[0], Addi, AddiU);
  or or_5 (or_5_out, Jr, output__decoder_signal[0], Beq, Bne, Bqtz, output__WriteMemory, J);
  or or_6 (output__RF_R1_RS_0_RT_1, Sll, Srl, Sra);
  not not_1 (output__RF_WF_RD_RT, or_7_out);
  or or_7 (or_7_out, output__extend_chose[0], output__extend_chose[1]);
  or OP3 (OP0_out[3], OR_3_out, Nor, Cmp_out, SltU, Equ_out);
  and and_11 (Bqtz, Input__im[26], Input__im[27], Input__im[28], ~Input__im[29], ~Input__im[30], ~Input__im[31]);  // AND_Gate
  and and_12 (output__decoder_signal[0], Class_R, ~Input__im[0], ~Input__im[1], Input__im[2], Input__im[3], ~Input__im[4], ~Input__im[5]);  // AND_Gate
  or or_8 (output__Alu_y, or_4_out, output__WriteMemory, or_1_out);
  not not_2 (output__RF_W_1_able, or_5_out);
  Multiplexer #(.width(4)) multiplexer_2 (
    .in0(4'b1111), .in1(4'b0001), .out(output__RF_Din_alu_dm_NPC_2), .sel(Lb));  // open: en
  and and_13 (Addi, ~Input__im[26], ~Input__im[27], ~Input__im[28], Input__im[29], ~Input__im[30], ~Input__im[31]);  // AND_Gate
  and and_14 (Add, Class_R, ~Input__im[0], ~Input__im[1], ~Input__im[2], ~Input__im[3], ~Input__im[4], Input__im[5]);  // AND_Gate
  or or_9 (output__IfJump, Bqtz, Bne, Beq);
  and and_15 (AddiU, Input__im[26], ~Input__im[27], ~Input__im[28], Input__im[29], ~Input__im[30], ~Input__im[31]);  // AND_Gate
  and and_16 (AddU, Class_R, Input__im[0], ~Input__im[1], ~Input__im[2], ~Input__im[3], ~Input__im[4], Input__im[5]);  // AND_Gate
  Comparator #(.width(6), .mode("unsigned")) comparator_1 (
    .a(Input__im[31:26]), .b(6'b000011), .gt(output__extend_chose[0]));  // open: eq, lt
  nor nor_1 (output__extend_chose[1], output__extend_chose[0], Class_R);
  and and_17 (Slti, ~Input__im[26], Input__im[27], ~Input__im[28], Input__im[29], ~Input__im[30], ~Input__im[31]);  // AND_Gate
  and and_18 (Sub, Class_R, ~Input__im[0], Input__im[1], ~Input__im[2], ~Input__im[3], ~Input__im[4], Input__im[5]);  // AND_Gate
  and and_19 (Andi, ~Input__im[26], ~Input__im[27], Input__im[28], Input__im[29], ~Input__im[30], ~Input__im[31]);  // AND_Gate
  and and_20 (SubU, Class_R, Input__im[0], Input__im[1], ~Input__im[2], ~Input__im[3], ~Input__im[4], Input__im[5]);  // AND_Gate
  or or_10 (or_10_out, Bqtz, Beq);
  or or_11 (output__npc_newpc_R1_lable, J, output__decoder_signal[1]);
  and and_21 (Ori, Input__im[26], ~Input__im[27], Input__im[28], Input__im[29], ~Input__im[30], ~Input__im[31]);  // AND_Gate
  and and_22 (And, Class_R, ~Input__im[0], ~Input__im[1], Input__im[2], ~Input__im[3], ~Input__im[4], Input__im[5]);  // AND_Gate
  or or_12 (or_12_out, Beq, Bne, Bqtz);
  and and_23 (output__extend_offset[1], Input__im[26], Input__im[27], Input__im[28], Input__im[29], ~Input__im[30], ~Input__im[31]);  // AND_Gate
  and and_24 (Or, Class_R, Input__im[0], ~Input__im[1], Input__im[2], ~Input__im[3], ~Input__im[4], Input__im[5]);  // AND_Gate
  and and_25 (and_25_out, or_10_out, input__alu_equal);
  and and_26 (and_26_out, Bne, ~input__alu_equal);  // AND_Gate
  or or_13 (output__extend_offset[0], or_12_out, output__extend_chose[1]);
  or or_14 (output__ReadMemory, Lw, Lb);
  and and_27 (Lb, ~Input__im[26], ~Input__im[27], ~Input__im[28], ~Input__im[29], ~Input__im[30], Input__im[31]);  // AND_Gate
  and and_28 (Nor, Class_R, Input__im[0], Input__im[1], Input__im[2], ~Input__im[3], ~Input__im[4], Input__im[5]);  // AND_Gate
  or or_15 (output__npc_chose_Off_new, J, output__decoder_signal[1], Jr);
  or or_16 (output__npc_offset_0_Extend, and_25_out, and_26_out);
  or or_17 (output__extend_i_iu, AddiU, Sll, Sra, Srl);
  and and_29 (Lw, Input__im[26], Input__im[27], ~Input__im[28], ~Input__im[29], ~Input__im[30], Input__im[31]);  // AND_Gate
  and and_30 (Slt, Class_R, ~Input__im[0], Input__im[1], ~Input__im[2], Input__im[3], ~Input__im[4], Input__im[5]);  // AND_Gate
  and and_31 (output__WriteMemory, Input__im[26], Input__im[27], ~Input__im[28], Input__im[29], ~Input__im[30], Input__im[31]);  // AND_Gate
  and and_32 (SltU, Class_R, Input__im[0], Input__im[1], ~Input__im[2], Input__im[3], ~Input__im[4], Input__im[5]);  // AND_Gate

  assign output__RF_Din_alu_dm_NPC[1] = output__decoder_signal[1];

  // Other names for the same wires on the sheet: Alu_op[3:0] = output__Alu_op; Alu_out = input__alu_equal;
  //   Alu_y = output__Alu_y; Class_I = output__extend_chose[0]; Ctext_chose[1:0] = output__extend_chose;
  //   Class_J = output__extend_chose[1]; Ctext_i_iu = output__extend_i_iu; Ctext_offset[1:0] = output__extend_offset;
  //   Lui = output__extend_offset[1]; CtIm[31:0] = Input__im; Im_fun[5:0] = Input__im[5:0];
  //   Im_op[5:0] = Input__im[31:26]; Decoder_signal[1:0] = output__decoder_signal;
  //   SysCall = output__decoder_signal[0]; Jal = output__decoder_signal[1];
  //   RF_Din[1:0] = {output__decoder_signal[1], output__RF_Din_alu_dm_NPC[0]}; IfJump = output__IfJump;
  //   MemoryMask[3:0] = output__RF_Din_alu_dm_NPC_2; Npc_chose = output__npc_chose_Off_new;
  //   Npc_NewPC = output__npc_newpc_R1_lable; Npc_Offset = output__npc_offset_0_Extend;
  //   ReadMemory = output__ReadMemory; RF_R1 = output__RF_R1_RS_0_RT_1; RF_W = output__RF_W_1_able;
  //   RF_WF = output__RF_WF_RD_RT; Sw = output__WriteMemory; WriteMemory = output__WriteMemory
endmodule

// Extend
module extend (
  input  [25:0] input__26bit,
  input  [1:0] input__offset,
  input  input__i_iu,
  input  [1:0] input__chose,
  output [31:0] \output 
);

  wire [2:2] not_1_out;
  wire [4:0] multiplexer_1_out;
  wire [31:0] bit_extender_1_out, bit_extender_2_out, bit_extender_3_out, bit_extender_4_out,
       bit_extender_5_out, bit_extender_6_out, multiplexer_2_out;

  assign bit_extender_1_out = {{6{1'b0}}, input__26bit};  // Bit_Extender bit_extender_1
  assign bit_extender_2_out = {{6{input__26bit[25]}}, input__26bit};  // Bit_Extender bit_extender_2
  assign bit_extender_3_out = {{16{1'b0}}, input__26bit[15:0]};  // Bit_Extender bit_extender_3
  assign bit_extender_4_out = {{16{input__26bit[15]}}, input__26bit[15:0]};  // Bit_Extender bit_extender_4
  not not_1 (not_1_out[2], input__i_iu);
  assign bit_extender_5_out = {{27{1'b0}}, input__26bit[10:6]};  // Bit_Extender bit_extender_5
  assign bit_extender_6_out = {{27{input__26bit[10]}}, input__26bit[10:6]};  // Bit_Extender bit_extender_6
  Multiplexer #(.select(2), .width(5)) multiplexer_1 (
    .in0({5{1'b0}}), .in1(5'b00010), .in2(5'b10000), .in3({5{1'b0}}), .out(multiplexer_1_out),
    .sel(input__offset));  // open: en
  Multiplexer #(.select(3), .width(32)) multiplexer_2 (
    .in0(bit_extender_5_out), .in1(bit_extender_3_out), .in2(bit_extender_1_out), .in3({32{1'b0}}),
    .in4(bit_extender_6_out), .in5(bit_extender_4_out), .in6(bit_extender_2_out), .in7({32{1'b0}}),
    .out(multiplexer_2_out), .sel({not_1_out[2], input__chose}));  // open: en
  Shifter #(.width(32)) shifter_1 (.in(multiplexer_2_out), .\dist (multiplexer_1_out), .out(\output ));

  // Other names for the same wires on the sheet: ext_chose[1:0] = input__chose; ext_Extend[31:0] = \output ;
  //   ext_i_iu = input__i_iu; ext_Imm[25:0] = input__26bit; ext_Imm16[15:0] = input__26bit[15:0];
  //   ext_shmat[4:0] = input__26bit[10:6]; ext_offset[1:0] = input__offset
endmodule

// Decoder
module Decode (
  input  [31:0] input__IF,
  input  [1:0] input__Signal_ord_syscall_jal,
  output [4:0] output__RS,
  output [4:0] output__RT,
  output [4:0] output__RD,
  output [25:0] output__im26
);

  wire [4:0] multiplexer_3_out;

  Multiplexer #(.width(5)) multiplexer_1 (
    .in0(input__IF[25:21]), .in1(5'b00010), .out(output__RS), .sel(input__Signal_ord_syscall_jal[0]));  // open: en
  Multiplexer #(.width(26)) multiplexer_2 (
    .in0(input__IF[25:0]), .in1(26'h280), .out(output__im26), .sel(input__Signal_ord_syscall_jal[0]));  // open: en
  Multiplexer #(.width(5)) multiplexer_3 (
    .in0(input__IF[20:16]), .in1(5'b00100), .out(multiplexer_3_out), .sel(input__Signal_ord_syscall_jal[0]));  // open: en
  Multiplexer #(.width(5)) multiplexer_4 (
    .in0(multiplexer_3_out), .in1({5{1'b1}}), .out(output__RT), .sel(input__Signal_ord_syscall_jal[1]));  // open: en

  assign output__RD = input__IF[15:11];

  // Other names for the same wires on the sheet: De_IF[31:0] = input__IF; De_Rd[4:0] = input__IF[15:11];
  //   De_im[25:0] = output__im26; De_Rs[4:0] = output__RS; De_Rt[4:0] = output__RT;
  //   De_signal[1:0] = input__Signal_ord_syscall_jal
endmodule

// Register \nFile
module register (
  input  [4:0] Input__Rw,
  input  [4:0] Input__R1,
  input  [31:0] Input__Din,
  input  [4:0] Input__R2,
  input  Input__W,
  input  clk,
  output [31:0] output__R2,
  output [31:0] output__R1
);

  // RegisterFile registerfile_1: pin names not known; wires that end beside it: Input__Din, clk, Input__W, Input__Rw, Input__R1, Input__R2, output__R1, output__R2

  // Other names for the same wires on the sheet: reg_Din[31:0] = Input__Din; reg_oR1[31:0] = output__R1;
  //   reg_oR2[31:0] = output__R2; reg_R1[4:0] = Input__R1; reg_R2[4:0] = Input__R2; reg_Rw[4:0] = Input__Rw;
  //   reg_we = Input__W
endmodule

// ALU
module Alu (
  input  [31:0] in_1,
  input  [31:0] in_2,
  input  [3:0] in_3,
  output [31:0] out_4
);

  ALU alu_1 (
    .AluOP(in_3), .X(in_1), .Result(out_4), .Y(in_2));  // open: Equal, Signed_Overflow, Result_2, UnSigned_Overflow
endmodule

// Couner
module Counter (
  input  in,
  input  clk,
  output [15:0] out
);

  wire [15:0] adder_1_out, bit_extender_1_out;

  assign bit_extender_1_out = {{15{1'b0}}, in};  // Bit_Extender bit_extender_1
  Adder #(.width(16)) adder_1 (.a(out), .b(bit_extender_1_out), .out(adder_1_out));  // open: cin, cout
  Register #(.width(16)) register_1 (.D(adder_1_out), .Q(out), .clk(clk));  // open: en, clr
endmodule
